# Fritzing sketch fritzing (saved by Fritzing 0.9.10b)
perfboards: 1

parts:
  U1 = SWITCH_SPDT [package=kps-1290]
  U2 = LuaNode32 / ESP32
  TRM1 = Borne kre 2 vias
  TRM2 = Borne kre 2 vias
  TRM3 = Borne kre 2 vias
  Componente1 = Motor Driver 1A Dual TB6612FNG
  U3 = Mini-360 DC-DC Buck converter [package=THT]

nets:
  N1: U1.O, TRM1.pin_1
  GND: U2.GND, Componente1.GND
  N2: U2.Vin, U3.OUT+
  3V3: U2.3V3, Componente1.VCC
  N3: U2.D4, Componente1.PWMA
  N4: U2.RX2, Componente1.AIN2
  N5: U2.TX2, Componente1.AIN1
  N6: U2.D5, Componente1.STBY
  N7: U2.D18, Componente1.BIN1
  N8: U2.D19, Componente1.BIN2
  N9: U2.D21, Componente1.PWMB
  N10: TRM1.pin_2, U3.IN-
  N11: TRM2.pin_1, Componente1.A02
  N12: TRM2.pin_2, Componente1.A01
  N13: TRM3.pin_1, Componente1.B01
  N14: TRM3.pin_2, Componente1.B02
  N15: Componente1.VM, U3.IN+

custom parts:
  LuaNode32 / ESP32: ESP32 based LuaNode32
  Borne kre 2 vias: 2-pin Terminal Block
  Mini-360 DC-DC Buck converter: Mini-360 DC-DC Buck converter. Tiny buck step down voltage converter, input voltage 4.75 to 23V output 1 to 17V adjustable. Available from ebay and the like.
