# Fritzing sketch fritzing (saved by Fritzing 0.9.10b)
perfboards: 1

parts:
  TRM1 = Borne kre 2 vias
  U1 = LuaNode32 / ESP32
  Componente1 = InvenSense MPU6050
  U2 = SWITCH_SPDT [package=kps-1290]

nets:
  N1: TRM1.pin_1, U2.S
  N2: TRM1.pin_2, U1.Vin
  N3: U1.GND, U2.P
  3V3: U1.3V3, Componente1.VCC
  N4: U1.D21, Componente1.SDA
  N5: U1.D22, Componente1.SCL

custom parts:
  Borne kre 2 vias: 2-pin Terminal Block
  LuaNode32 / ESP32: ESP32 based LuaNode32
