# Fritzing sketch circuit (saved by Fritzing 0.9.10b)
perfboards: 2

parts:
  DFRobot_DFPlayer_Mini2 = DFRobot DFPlayer Mini [part_number=DFR0299]
  S2 = Momentary Switch [package=ksa_sealed_tac_switch]
  R2 = Resistor [tolerance=±5% resistance=220 package="0805 [SMD]"]
  Componente3 = Arduino Nano (Rev3.0)
  J3 = JST XH 2A male [form="♂ (male)" package=THT]
  J4 = JST XH 2A male [form="♂ (male)" package=THT]
  U1 = Mini-360 DC-DC Buck converter [package=THT]
  Componente4 = Arduino Nano (Rev3.0)
  DFRobot_DFPlayer_Mini3 = DFRobot DFPlayer Mini [part_number=DFR0299]
  R3 = Resistor [tolerance=±5% resistance=220 package="0805 [SMD]"]
  TRM1 = Borne kre 2 vias
  TRM2 = Borne kre 2 vias
  S4 = Momentary Switch [package=ksa_sealed_tac_switch]

nets:
  VCC: DFRobot_DFPlayer_Mini2.VCC, Componente3.5V
  N1: DFRobot_DFPlayer_Mini2.RX, Componente3.A5
  N2: DFRobot_DFPlayer_Mini2.TX, Componente3.A4
  N3: DFRobot_DFPlayer_Mini2.SPK_1, J4.pin2
  N4: DFRobot_DFPlayer_Mini2.GND-1, DFRobot_DFPlayer_Mini2.GND-2
  N5: DFRobot_DFPlayer_Mini2.SPK_2, J4.pin1
  N6: S2.1, Componente3.A3
  N7: S2.3, J3.pin1
  N8: S2.4, Componente3.GND
  N9: R2.Pin_1, Componente3.A6
  N10: Componente3.VIN, J3.pin2
  N11: U1.IN-, U1.OUT-
  N12: U1.IN+, Componente4.VIN, TRM2.pin_1
  N13: U1.OUT+, DFRobot_DFPlayer_Mini3.VCC
  N14: Componente4.GND, DFRobot_DFPlayer_Mini3.GND-1, DFRobot_DFPlayer_Mini3.GND-2, TRM2.pin_2, S4.1
  N15: Componente4.A6, R3.Pin_1
  N16: Componente4.A4, DFRobot_DFPlayer_Mini3.TX
  N17: Componente4.A0, S4.4
  N18: DFRobot_DFPlayer_Mini3.RX, R3.Pin_0
  N19: DFRobot_DFPlayer_Mini3.SPK_1, TRM1.pin_2
  N20: DFRobot_DFPlayer_Mini3.SPK_2, TRM1.pin_1

custom parts:
  JST XH 2A male: JST XH-2A
  Mini-360 DC-DC Buck converter: Mini-360 DC-DC Buck converter. Tiny buck step down voltage converter, input voltage 4.75 to 23V output 1 to 17V adjustable. Available from ebay and the like.
  Borne kre 2 vias: 2-pin Terminal Block
